# Fritzing sketch wiring_diagram (saved by Fritzing 0.9.3b)
breadboards: 1

parts:
  Part1 = Photon
  U4 = RELAY-SOLIDSTATE [package=relay-s108t02]
  F1 = FUSE [package=fuse_5mm]
  HLK-PM1 = HLK-PM01
  LCD2 = LCD screen  # not connected
  J2 = screw terminal, 4 pins
  J4 = screw terminal, 3 pins
  J5 = screw terminal, 3 pins
  S4 = Round Pushbutton
  LED1 = LED - 3mm [color="Green (565nm)" package="3 mm [THT]"]
  R1 = Resistor [tolerance=±5% resistance=100 package="2010 [SMD]"]
  J6 = screw terminal, 4 pins
  X1 = DB9 Connector [package=db9]  # not connected

nets:
  N1: Part1.RX, J6.pin2
  N2: Part1.TX, J6.pin3
  N3: Part1.GND, U4.-, HLK-PM1.-Vo, J2.pin1, S4.leg0, LED1.cathode, J6.pin1
  N4: Part1.VIN, HLK-PM1.+Vo, J2.pin2, J6.pin4
  N5: Part1.D0, J2.pin3
  N6: Part1.D1, J2.pin4
  N7: Part1.D4, R1.Pin_1
  N8: Part1.D5, S4.leg1
  N9: Part1.D6, U4.+
  N10: U4.T1, F1.1, HLK-PM1.AC#1
  N11: U4.T2, J4.pin1
  N12: F1.2, J5.pin1
  N13: HLK-PM1.AC#0, J4.pin2, J5.pin2
  N14: J4.pin3, J5.pin3
  N15: LED1.anode, R1.Pin_0

notes:
  AC power in
  G (ground)
  N (neutral)
  L (live)
  LCD Backpack
  GND
  VCC
  SDA
  SCL
  AC to Spec20
  G (ground)
  N (neutral)
  L (live)
  push button (pulled high)
  with integrated LED (2.2V)
  RS232 converter
  with male DB9
  VCC
  <--
  -->
  GND
